# Fritzing sketch aspide-cabling (saved by Fritzing 1.0.6)
breadboards: 1

parts:
  Part1 = Adafruit QT Py ESP32 Pico [mn=Adafruit mpn="Adafruit #5395" part_number="Adafruit #5395"]
  Part2 = Adafruit I2C QT Rotary Encoder [part_number="Adafruit #4991"]
  NEOPIXEL1 = Neopixel Strip -- Black (30/m) [part_number=1376]

nets:
  GND: Part1.GND, Part2.GND, NEOPIXEL1.GND
  3.3V: Part1.3.3V, Part2.VCC
  N1: Part1.SDA1, Part2.SDA
  N2: Part1.SCL1, Part2.SCL
  N3: Part1.A1, NEOPIXEL1.Din
  +5V: Part1.+5V, NEOPIXEL1.+5V

custom parts:
  Adafruit I2C QT Rotary Encoder: Rotary encoders are soooo much fun! Twist em this way, then twist them that way. Unlike potentiometers, they go all the way around, and often have little detents for tactile feedback. But, if you've ever tried to add encoders to your project you know that they're a real challenge to use: timers, interrupts, debouncing... This Stemma QT breakout makes all that frustration go away - solder in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
  Neopixel Strip -- Black (30/m): These NeoPixel strips have 30 digitally-addressable pixel LEDs per meter and are very affordable and are only 12.5 mm wide, 10 mm if you remove the strip from the casing.
